// Logisim project final.circ as structural Verilog: 23 circuits, main circuit DataPathROM
module DataPathROM (
  output [31:0] Result
);

  wire and_1_out, BEQcontrol, CLKT, controllogicrom_1_bselect, controllogicrom_1_regwen,
       controllogicrom_1_wbselect, controllogicrom_1_wemem, ZeroFlagg;
  wire [2:0] controllogicrom_1_lselect, immselect;
  wire [3:0] controllogicrom_1_aluselecting;
  wire [4:0] rdi, rs1, rs2;
  wire [7:0] bitselector_1_out, shifter_1_out;
  wire [31:0] ALUop, imm_1_imm31_0, multiplexer_1_out, multiplexer_2_out, pc_1_outinstruction, ram_1_dout,
       registerfile_1_rs2, RS1T;

  Clock clock_1 (.out(CLKT));
  and and_1 (and_1_out, BEQcontrol, ZeroFlagg);
  IMM imm_1 (
    .Ins({pc_1_outinstruction[31:25], rs2, rs1, pc_1_outinstruction[14:12], rdi, pc_1_outinstruction[6:0]}),
    .selecting(immselect), .imm31_0(imm_1_imm31_0));
  PC pc_1 (
    .Clk(CLKT), .PCsrc(and_1_out), .Boffset(imm_1_imm31_0),
    .outInstruction({pc_1_outinstruction[31:25], rs2, rs1, pc_1_outinstruction[14:12], rdi, pc_1_outinstruction[6:0]}));
  RegisterFile registerfile_1 (
    .rsi1(rs1), .rsi2(rs2), .rdi(rdi), .rd(Result), .we(controllogicrom_1_regwen), .Clk(CLKT), .rs1(RS1T),
    .rs2(registerfile_1_rs2));
  ControlLogicROM controllogicrom_1 (
    .Instruction({pc_1_outinstruction[31:25], rs2, rs1, pc_1_outinstruction[14:12], rdi, pc_1_outinstruction[6:0]}),
    .ALUselecting(controllogicrom_1_aluselecting), .RegWen(controllogicrom_1_regwen),
    .wbselect(controllogicrom_1_wbselect), .Bselect(controllogicrom_1_bselect), .immSelect(immselect),
    .lselect(controllogicrom_1_lselect), .WEmem(controllogicrom_1_wemem), .BEQ(BEQcontrol));
  BitSelector #(.group(8), .width(32)) bitselector_1 (.in(ALUop), .out(bitselector_1_out), .sel(2'b00));
  Multiplexer #(.width(32)) multiplexer_1 (
    .in0(ALUop), .in1(RS1T), .out(multiplexer_1_out), .sel(controllogicrom_1_wemem));
  Multiplexer #(.width(32)) multiplexer_2 (
    .in0(registerfile_1_rs2), .in1(imm_1_imm31_0), .out(multiplexer_2_out), .sel(controllogicrom_1_bselect));
  Shifter #(.shift("lr")) shifter_1 (.in(bitselector_1_out), .\dist (3'b010), .out(shifter_1_out));
  RAM #(.dataWidth(32), .enables("line"), .misaligned("true"), .\type ("nonvolatile")) ram_1 (
    .addr(shifter_1_out), .we(controllogicrom_1_wemem), .clk(CLKT), .din(multiplexer_1_out), .dout(ram_1_dout));
  ALU alu_1 (.DataA(RS1T), .DataB(multiplexer_2_out), .Selecting(controllogicrom_1_aluselecting), .DataD(ALUop));
  Zeroflag zeroflag_1 (.inputZero(ALUop), .zero_Flag(ZeroFlagg));
  LoadCrtl loadcrtl_1 (
    .A(ALUop), .lw(ram_1_dout), .lSelect(controllogicrom_1_lselect), .wbselect(controllogicrom_1_wbselect),
    .Data(Result));

  // Other names for the same wires on the sheet: OutPutT[31:0] = Result
endmodule

module PC (
  input  Clk,
  input  PCsrc,
  input  [31:0] Boffset,
  output [31:0] outInstruction
);

  wire [31:0] InPCT, multiplexer_1_out, OutPCT;

  Register #(.width(32)) register_1 (.D(InPCT), .en(1'b1), .clk(Clk), .Q(OutPCT));  // open: clr
  Multiplexer #(.width(32)) multiplexer_1 (.in0(32'h1), .in1(Boffset), .out(multiplexer_1_out), .sel(PCsrc));
  Adder #(.width(32)) adder_1 (.a(OutPCT), .b(multiplexer_1_out), .out(InPCT));  // open: cin, cout
  IM im_1 (.ADDR(OutPCT), .out_2(outInstruction));

  // Other names for the same wires on the sheet: ClkT = Clk
endmodule

module RegisterFile (
  input  [4:0] rsi1,
  input  [4:0] rsi2,
  input  [4:0] rdi,
  input  [31:0] rd,
  input  we,
  input  Clk,
  output [31:0] rs1,
  output [31:0] rs2
);

  wire x0weT, x1weT, x2weT, x3weT, x4weT, x5weT, x6weT, x7weT, x8weT, x9weT, x10weT, x11weT, x12weT, x13weT,
       x14weT, x15weT, x16weT, x17weT, x18weT, x19weT, x20weT, x21weT, x22weT, x23weT, x24weT, x25weT,
       x26weT, x27weT, x28weT, x29weT, x30weT, x31weT;
  wire [31:0] x0qT, x1qT, x2qT, x3qT, x4qT, x5qT, x6qT, x7qT, x8qT, x9qT, x10qT, x11qT, x12qT, x13qT, x14qT,
       x15qT, x16qT, x17qT, x18qT, x19qT, x20qT, x21qT, x22qT, x23qT, x24qT, x25qT, x26qT, x27qT, x28qT,
       x29qT, x30qT, x31qT;

  Register #(.width(32)) x0 (.D(rd), .en(x0weT), .clk(Clk), .Q(x0qT));  // open: clr
  Register #(.width(32)) x4 (.D(rd), .en(x4weT), .clk(Clk), .Q(x4qT));  // open: clr
  Register #(.width(32)) x8 (.D(rd), .en(x8weT), .clk(Clk), .Q(x8qT));  // open: clr
  Register #(.width(32)) x12 (.D(rd), .en(x12weT), .clk(Clk), .Q(x12qT));  // open: clr
  Register #(.width(32)) x16 (.D(rd), .en(x16weT), .clk(Clk), .Q(x16qT));  // open: clr
  Register #(.width(32)) x20 (.D(rd), .en(x20weT), .clk(Clk), .Q(x20qT));  // open: clr
  Register #(.width(32)) x24 (.D(rd), .en(x24weT), .clk(Clk), .Q(x24qT));  // open: clr
  Register #(.width(32)) x28 (.D(rd), .en(x28weT), .clk(Clk), .Q(x28qT));  // open: clr
  Register #(.width(32)) x1 (.D(rd), .en(x1weT), .clk(Clk), .Q(x1qT));  // open: clr
  Register #(.width(32)) x5 (.D(rd), .en(x5weT), .clk(Clk), .Q(x5qT));  // open: clr
  Register #(.width(32)) x9 (.D(rd), .en(x9weT), .clk(Clk), .Q(x9qT));  // open: clr
  Register #(.width(32)) x13 (.D(rd), .en(x13weT), .clk(Clk), .Q(x13qT));  // open: clr
  Register #(.width(32)) x17 (.D(rd), .en(x17weT), .clk(Clk), .Q(x17qT));  // open: clr
  Register #(.width(32)) x21 (.D(rd), .en(x21weT), .clk(Clk), .Q(x21qT));  // open: clr
  Register #(.width(32)) x25 (.D(rd), .en(x25weT), .clk(Clk), .Q(x25qT));  // open: clr
  Register #(.width(32)) x29 (.D(rd), .en(x29weT), .clk(Clk), .Q(x29qT));  // open: clr
  Register #(.width(32)) x2 (.D(rd), .en(x2weT), .clk(Clk), .Q(x2qT));  // open: clr
  Register #(.width(32)) x6 (.D(rd), .en(x6weT), .clk(Clk), .Q(x6qT));  // open: clr
  Register #(.width(32)) x10 (.D(rd), .en(x10weT), .clk(Clk), .Q(x10qT));  // open: clr
  Register #(.width(32)) x14 (.D(rd), .en(x14weT), .clk(Clk), .Q(x14qT));  // open: clr
  Register #(.width(32)) x18 (.D(rd), .en(x18weT), .clk(Clk), .Q(x18qT));  // open: clr
  Register #(.width(32)) x22 (.D(rd), .en(x22weT), .clk(Clk), .Q(x22qT));  // open: clr
  Register #(.width(32)) x26 (.D(rd), .en(x26weT), .clk(Clk), .Q(x26qT));  // open: clr
  Register #(.width(32)) x30 (.D(rd), .en(x30weT), .clk(Clk), .Q(x30qT));  // open: clr
  Register #(.width(32)) x3 (.D(rd), .en(x3weT), .clk(Clk), .Q(x3qT));  // open: clr
  Register #(.width(32)) x7 (.D(rd), .en(x7weT), .clk(Clk), .Q(x7qT));  // open: clr
  Register #(.width(32)) x11 (.D(rd), .en(x11weT), .clk(Clk), .Q(x11qT));  // open: clr
  Register #(.width(32)) x15 (.D(rd), .en(x15weT), .clk(Clk), .Q(x15qT));  // open: clr
  Register #(.width(32)) x19 (.D(rd), .en(x19weT), .clk(Clk), .Q(x19qT));  // open: clr
  Register #(.width(32)) x23 (.D(rd), .en(x23weT), .clk(Clk), .Q(x23qT));  // open: clr
  Register #(.width(32)) x27 (.D(rd), .en(x27weT), .clk(Clk), .Q(x27qT));  // open: clr
  Register #(.width(32)) x31 (.D(rd), .en(x31weT), .clk(Clk), .Q(x31qT));  // open: clr
  Demultiplexer #(.select(5)) demultiplexer_1 (
    .out0(x0weT), .out1(x1weT), .out2(x2weT), .out3(x3weT), .out4(x4weT), .out5(x5weT), .out6(x6weT),
    .out7(x7weT), .out8(x8weT), .out9(x9weT), .out10(x10weT), .out11(x11weT), .out12(x12weT), .out13(x13weT),
    .out14(x14weT), .out15(x15weT), .out16(x16weT), .out17(x17weT), .out18(x18weT), .out19(x19weT),
    .out20(x20weT), .out21(x21weT), .out22(x22weT), .out23(x23weT), .out24(x24weT), .out25(x25weT),
    .out26(x26weT), .out27(x27weT), .out28(x28weT), .out29(x29weT), .out30(x30weT), .out31(x31weT), .in(we),
    .sel(rdi));
  Multiplexer #(.select(5), .width(32)) multiplexer_1 (
    .in0(x0qT), .in1(x1qT), .in2(x2qT), .in3(x3qT), .in4(x4qT), .in5(x5qT), .in6(x6qT), .in7(x7qT),
    .in8(x8qT), .in9(x9qT), .in10(x10qT), .in11(x11qT), .in12(x12qT), .in13(x13qT), .in14(x14qT),
    .in15(x15qT), .in16(x16qT), .in17(x17qT), .in18(x18qT), .in19(x19qT), .in20(x20qT), .in21(x21qT),
    .in22(x22qT), .in23(x23qT), .in24(x24qT), .in25(x25qT), .in26(x26qT), .in27(x27qT), .in28(x28qT),
    .in29(x29qT), .in30(x30qT), .in31(x31qT), .out(rs1), .sel(rsi1));
  Multiplexer #(.select(5), .width(32)) multiplexer_2 (
    .in0(x0qT), .in1(x1qT), .in2(x2qT), .in3(x3qT), .in4(x4qT), .in5(x5qT), .in6(x6qT), .in7(x7qT),
    .in8(x8qT), .in9(x9qT), .in10(x10qT), .in11(x11qT), .in12(x12qT), .in13(x13qT), .in14(x14qT),
    .in15(x15qT), .in16(x16qT), .in17(x17qT), .in18(x18qT), .in19(x19qT), .in20(x20qT), .in21(x21qT),
    .in22(x22qT), .in23(x23qT), .in24(x24qT), .in25(x25qT), .in26(x26qT), .in27(x27qT), .in28(x28qT),
    .in29(x29qT), .in30(x30qT), .in31(x31qT), .out(rs2), .sel(rsi2));

  // Other names for the same wires on the sheet: ClkT = Clk; rdiT[4:0] = rdi; rdT[31:0] = rd; rs1T[31:0] = rs1;
  //   rs2T[31:0] = rs2; rsi1T[4:0] = rsi1; rsi2T[4:0] = rsi2; weT = we
endmodule

module ALU (
  input  [31:0] DataA,
  input  [31:0] DataB,
  input  [3:0] Selecting,
  output [31:0] DataD
);

  wire branch_1_breq, comparator_1_lt, comparator_2_lt;
  wire [31:0] addOut, andOut, brOut, orOut, sllOut, sltOut, sltuOut, sraOut, srlOut, subOut, xorOut;

  Shifter #(.shift("ar"), .width(32)) shifter_1 (.in(DataA), .\dist (DataB[4:0]), .out(sraOut));
  Adder #(.width(32)) adder_1 (.a(DataA), .b(DataB), .out(addOut));  // open: cin, cout
  Subtractor #(.width(32)) subtractor_1 (.a(DataA), .b(DataB), .out(subOut));  // open: bin, bout
  Shifter #(.width(32)) shifter_2 (.in(DataA), .\dist (DataB[4:0]), .out(sllOut));
  Comparator #(.width(32)) comparator_1 (.a(DataA), .b(DataB), .lt(comparator_1_lt));  // open: gt, eq
  Comparator #(.mode("unsigned"), .width(32)) comparator_2 (
    .a(DataA), .b(DataB), .lt(comparator_2_lt));  // open: gt, eq
  Shifter #(.shift("lr"), .width(32)) shifter_3 (.in(DataA), .\dist (DataB[4:0]), .out(srlOut));
  assign orOut = DataA | DataB;  // OR_Gate or_1, 32 bits wide
  assign andOut = DataA & DataB;  // AND_Gate and_1, 32 bits wide
  assign xorOut = DataA ^ DataB;  // XOR_Gate xor_1, 32 bits wide
  assign sltOut = {{31{1'b0}}, comparator_1_lt};  // Bit_Extender bit_extender_1
  assign sltuOut = {{31{1'b0}}, comparator_2_lt};  // Bit_Extender bit_extender_2
  Branch branch_1 (.DataA(DataA), .DataB(DataB), .brEq(branch_1_breq));
  assign brOut = {{31{1'b0}}, branch_1_breq};  // Bit_Extender bit_extender_3
  Multiplexer #(.select(4), .width(32)) multiplexer_1 (
    .in0(addOut), .in1(sllOut), .in2(sltOut), .in3(sltuOut), .in4(xorOut), .in5(srlOut), .in6(orOut),
    .in7(andOut), .in8(subOut), .in13(brOut), .out(DataD), .sel(Selecting));  // open: in9, in10, in11, in12, in14, in15

  // Other names for the same wires on the sheet: DataAT[31:0] = DataA; DataBL5T[4:0] = DataB[4:0];
  //   DataBT[31:0] = DataB; DataDT[31:0] = DataD; selT[3:0] = Selecting

  // Notes on the sheet:
  //   add 0000, sub 1000 , sll 0001 , slt 0010 , srl 0101 , or 0110 , and 0111 , xor 0100 , sra:beq 1101, sltu 0011
endmodule

module Branch (
  input  [31:0] DataA,
  input  [31:0] DataB,
  output brEq
);

  Comparator #(.width(32)) comparator_1 (.a(DataA), .b(DataB), .eq(brEq));  // open: gt, lt

  // Other names for the same wires on the sheet: brEqT = brEq; DataAT[31:0] = DataA; DataBT[31:0] = DataB
endmodule

module IMM (
  input  [31:0] Ins,
  input  [2:0] selecting,
  output [31:0] imm31_0
);

  wire [3:0] bsplitor_1_imm4_1;
  wire [4:0] ssplitor_1_imm4_0;
  wire [5:0] bsplitor_1_imm10_5;
  wire [6:0] ssplitor_1_imm11_5;
  wire [7:0] jsplitor_1_imm19_12;
  wire [9:0] jsplitor_1_imm10_1;
  wire [11:0] isplitor_1_imm11_0;
  wire [12:11] bsplitor_1_imm11;
  wire [20:11] jsplitor_1_imm11;
  wire [31:0] BoutT, IoutT, JoutT, SoutT;
  wire [31:12] UoutT;

  Isplitor isplitor_1 (.Instroction(Ins), .imm11_0(isplitor_1_imm11_0));  // open: opcode, rd, funct3, rs1
  Ssplitor ssplitor_1 (
    .Instruction(Ins), .imm4_0(ssplitor_1_imm4_0), .imm11_5(ssplitor_1_imm11_5));  // open: opcode, funct3, rs1, rs2
  Bsplitor bsplitor_1 (
    .Ins(Ins), .imm11(bsplitor_1_imm11[11]), .imm4_1(bsplitor_1_imm4_1), .imm10_5(bsplitor_1_imm10_5),
    .imm12(bsplitor_1_imm11[12]));  // open: opcdoe, funct3, rs1, rs2
  Jsplitor jsplitor_1 (
    .Ins(Ins), .imm19_12(jsplitor_1_imm19_12), .imm11(jsplitor_1_imm11[11]), .imm10_1(jsplitor_1_imm10_1),
    .imm20(jsplitor_1_imm11[20]));  // open: opcode, rd
  Usplitor usplitor_1 (.Instruction(Ins), .imm31_12(UoutT));  // open: opcode, rd
  assign IoutT = {{20{isplitor_1_imm11_0[11]}}, isplitor_1_imm11_0};  // Bit_Extender bit_extender_1
  assign SoutT = {{20{ssplitor_1_imm11_5[6]}}, {ssplitor_1_imm11_5, ssplitor_1_imm4_0}};  // Bit_Extender bit_extender_2
  assign BoutT = {{19{bsplitor_1_imm11[12]}}, {bsplitor_1_imm11, bsplitor_1_imm10_5, bsplitor_1_imm4_1, 1'b0}};  // Bit_Extender bit_extender_3
  assign JoutT = {{11{jsplitor_1_imm11[20]}}, {jsplitor_1_imm11[20], jsplitor_1_imm19_12, jsplitor_1_imm11[11], jsplitor_1_imm10_1, 1'b0}};  // Bit_Extender bit_extender_4
  Multiplexer #(.select(3), .width(32)) multiplexer_1 (
    .in0(IoutT), .in1(SoutT), .in2(BoutT), .in3(JoutT), .in4({UoutT, {12{1'b0}}}), .out(imm31_0),
    .sel(selecting));  // open: in5, in6, in7

  // Other names for the same wires on the sheet: imm31_0T[31:0] = imm31_0; InsT[31:0] = Ins;
  //   SelectingT[2:0] = selecting
endmodule

module Rsplitor (
  input  [31:0] Instruction,
  output [6:0] opcode,
  output [4:0] rd,
  output [2:0] funct3,
  output [4:0] rs1,
  output [4:0] rs2,
  output [6:0] funct7
);


  assign funct3 = Instruction[14:12];
  assign funct7 = Instruction[31:25];
  assign opcode = Instruction[6:0];
  assign rd = Instruction[11:7];
  assign rs1 = Instruction[19:15];
  assign rs2 = Instruction[24:20];
endmodule

module Isplitor (
  input  [31:0] Instroction,
  output [6:0] opcode,
  output [4:0] rd,
  output [2:0] funct3,
  output [4:0] rs1,
  output [11:0] imm11_0
);


  assign funct3 = Instroction[14:12];
  assign imm11_0 = Instroction[31:20];
  assign opcode = Instroction[6:0];
  assign rd = Instroction[11:7];
  assign rs1 = Instroction[19:15];
endmodule

module Ssplitor (
  input  [31:0] Instruction,
  output [6:0] opcode,
  output [4:0] imm4_0,
  output [2:0] funct3,
  output [4:0] rs1,
  output [4:0] rs2,
  output [6:0] imm11_5
);


  assign funct3 = Instruction[14:12];
  assign imm4_0 = Instruction[11:7];
  assign imm11_5 = Instruction[31:25];
  assign opcode = Instruction[6:0];
  assign rs1 = Instruction[19:15];
  assign rs2 = Instruction[24:20];
endmodule

module Usplitor (
  input  [31:0] Instruction,
  output [6:0] opcode,
  output [4:0] rd,
  output [19:0] imm31_12
);


  assign imm31_12 = Instruction[31:12];
  assign opcode = Instruction[6:0];
  assign rd = Instruction[11:7];
endmodule

module Bsplitor (
  input  [31:0] Ins,
  output [6:0] opcdoe,
  output imm11,
  output [3:0] imm4_1,
  output [2:0] funct3,
  output [4:0] rs1,
  output [4:0] rs2,
  output [5:0] imm10_5,
  output imm12
);


  assign funct3 = Ins[14:12];
  assign imm4_1 = Ins[11:8];
  assign imm10_5 = Ins[30:25];
  assign imm11 = Ins[7];
  assign imm12 = Ins[31];
  assign opcdoe = Ins[6:0];
  assign rs1 = Ins[19:15];
  assign rs2 = Ins[24:20];
endmodule

module Jsplitor (
  input  [31:0] Ins,
  output [6:0] opcode,
  output [4:0] rd,
  output [7:0] imm19_12,
  output imm11,
  output [9:0] imm10_1,
  output imm20
);


  assign imm10_1 = Ins[30:21];
  assign imm11 = Ins[20];
  assign imm19_12 = Ins[19:12];
  assign imm20 = Ins[31];
  assign opcode = Ins[6:0];
  assign rd = Ins[11:7];
endmodule

module FullAdder (
  input  in_1,
  input  in_2,
  input  in_3,
  input  in_4,
  input  in_5,
  input  in_6,
  input  in_7,
  input  in_8,
  input  in_9,
  input  in_10,
  input  A,
  input  in_12,
  input  in_13,
  input  in_14,
  input  in_15,
  input  B,
  input  in_17,
  input  in_18,
  input  in_19,
  input  in_20,
  input  in_21,
  input  in_22,
  input  in_23,
  input  in_24,
  input  in_25,
  input  in_26,
  input  in_27,
  input  in_28,
  input  in_29,
  input  in_30,
  input  in_31,
  input  in_32,
  input  in_33,
  input  in_34,
  input  in_35,
  input  in_36,
  input  in_37,
  input  in_38,
  input  in_39,
  input  in_40,
  input  in_41,
  input  in_42,
  input  in_43,
  input  in_44,
  input  in_45,
  input  in_46,
  input  in_47,
  input  in_48,
  input  in_49,
  input  in_50,
  input  in_51,
  input  in_52,
  input  in_53,
  input  in_54,
  input  in_55,
  input  in_56,
  input  in_57,
  input  in_58,
  input  in_59,
  input  in_60,
  input  in_61,
  input  in_62,
  input  in_63,
  input  in_64,
  input  [31:0] DataB,
  input  [31:0] DataA,
  output out_67,
  output out_68,
  output out_69,
  output out_70,
  output out_71,
  output out_72,
  output out_73,
  output out_74,
  output out_75,
  output out_76,
  output out_77,
  output out_78,
  output out_79,
  output out_80,
  output out_81,
  output out_82,
  output out_83,
  output out_84,
  output out_85,
  output out_86,
  output out_87,
  output out_88,
  output out_89,
  output out_90,
  output out_91,
  output out_92,
  output out_93,
  output out_94,
  output out_95,
  output out_96,
  output out_97,
  output out_98,
  output out_99
);

  wire and_1_out, and_2_out, and_3_out, and_4_out, and_5_out, and_6_out, and_7_out, and_8_out, and_9_out,
       and_10_out, and_11_out, and_12_out, and_13_out, and_14_out, and_15_out, and_16_out, and_17_out,
       and_18_out, and_19_out, and_20_out, and_21_out, and_22_out, and_23_out, and_24_out, and_25_out,
       and_26_out, and_27_out, and_28_out, and_29_out, and_30_out, and_31_out, and_32_out, and_33_out,
       and_34_out, and_35_out, and_36_out, and_37_out, and_38_out, and_39_out, and_40_out, and_41_out,
       and_42_out, and_43_out, and_44_out, and_45_out, and_46_out, and_47_out, and_48_out, and_49_out,
       and_50_out, and_51_out, and_52_out, and_53_out, and_54_out, and_55_out, and_56_out, and_57_out,
       and_58_out, and_59_out, and_60_out, and_61_out, and_62_out, and_63_out, and_64_out, or_1_out,
       or_2_out, or_3_out, or_4_out, or_5_out, or_6_out, or_7_out, or_8_out, or_9_out, or_10_out, or_11_out,
       or_12_out, or_13_out, or_14_out, or_15_out, or_16_out, or_17_out, or_18_out, or_19_out, or_20_out,
       or_21_out, or_22_out, or_23_out, or_24_out, or_25_out, or_26_out, or_27_out, or_28_out, or_29_out,
       or_30_out, or_31_out, xor_1_out, xor_2_out, xor_3_out, xor_4_out, xor_9_out, xor_10_out, xor_11_out,
       xor_12_out, xor_17_out, xor_18_out, xor_19_out, xor_20_out, xor_25_out, xor_26_out, xor_27_out,
       xor_28_out, xor_33_out, xor_34_out, xor_35_out, xor_36_out, xor_41_out, xor_42_out, xor_43_out,
       xor_44_out, xor_49_out, xor_50_out, xor_51_out, xor_52_out, xor_57_out, xor_58_out, xor_59_out,
       xor_60_out;

  and and_1 (and_1_out, 1'b0, xor_1_out);
  and and_2 (and_2_out, or_29_out, xor_2_out);
  and and_3 (and_3_out, or_30_out, xor_3_out);
  and and_4 (and_4_out, or_31_out, xor_4_out);
  xor xor_1 (xor_1_out, A, B);
  and and_5 (and_5_out, A, B);
  xor xor_2 (xor_2_out, in_27, in_32);
  and and_6 (and_6_out, in_27, in_32);
  xor xor_3 (xor_3_out, in_43, in_48);
  and and_7 (and_7_out, in_43, in_48);
  xor xor_4 (xor_4_out, in_59, in_64);
  and and_8 (and_8_out, in_59, in_64);
  or or_1 (or_1_out, and_5_out, and_1_out);
  or or_2 (or_2_out, and_6_out, and_2_out);
  or or_3 (or_3_out, and_7_out, and_3_out);
  or or_4 (or_4_out, and_8_out, and_4_out);
  xor xor_5 (out_74, xor_1_out, 1'b0);
  xor xor_6 (out_82, xor_2_out, or_29_out);
  xor xor_7 (out_90, xor_3_out, or_30_out);
  xor xor_8 (out_98, xor_4_out, or_31_out);
  and and_9 (and_9_out, or_1_out, xor_9_out);
  and and_10 (and_10_out, or_2_out, xor_10_out);
  and and_11 (and_11_out, or_3_out, xor_11_out);
  and and_12 (and_12_out, or_4_out, xor_12_out);
  xor xor_9 (xor_9_out, in_7, in_14);
  and and_13 (and_13_out, in_7, in_14);
  xor xor_10 (xor_10_out, in_23, in_30);
  and and_14 (and_14_out, in_23, in_30);
  xor xor_11 (xor_11_out, in_39, in_46);
  and and_15 (and_15_out, in_39, in_46);
  xor xor_12 (xor_12_out, in_55, in_62);
  and and_16 (and_16_out, in_55, in_62);
  or or_5 (or_5_out, and_13_out, and_9_out);
  or or_6 (or_6_out, and_14_out, and_10_out);
  or or_7 (or_7_out, and_15_out, and_11_out);
  or or_8 (or_8_out, and_16_out, and_12_out);
  xor xor_13 (out_72, xor_9_out, or_1_out);
  xor xor_14 (out_80, xor_10_out, or_2_out);
  xor xor_15 (out_88, xor_11_out, or_3_out);
  xor xor_16 (out_96, xor_12_out, or_4_out);
  xor xor_17 (xor_17_out, in_8, in_15);
  and and_17 (and_17_out, in_8, in_15);
  and and_18 (and_18_out, or_5_out, xor_17_out);
  and and_19 (and_19_out, or_6_out, xor_19_out);
  xor xor_18 (xor_18_out, in_40, in_47);
  and and_20 (and_20_out, in_40, in_47);
  and and_21 (and_21_out, or_7_out, xor_18_out);
  and and_22 (and_22_out, or_8_out, xor_20_out);
  xor xor_19 (xor_19_out, in_24, in_31);
  and and_23 (and_23_out, in_24, in_31);
  xor xor_20 (xor_20_out, in_56, in_63);
  and and_24 (and_24_out, in_56, in_63);
  xor xor_21 (out_73, xor_17_out, or_5_out);
  or or_9 (or_9_out, and_17_out, and_18_out);
  or or_10 (or_10_out, and_23_out, and_19_out);
  xor xor_22 (out_89, xor_18_out, or_7_out);
  or or_11 (or_11_out, and_20_out, and_21_out);
  or or_12 (or_12_out, and_24_out, and_22_out);
  xor xor_23 (out_81, xor_19_out, or_6_out);
  xor xor_24 (out_97, xor_20_out, or_8_out);
  xor xor_25 (xor_25_out, in_5, in_13);
  and and_25 (and_25_out, in_5, in_13);
  and and_26 (and_26_out, or_9_out, xor_25_out);
  and and_27 (and_27_out, or_10_out, xor_27_out);
  xor xor_26 (xor_26_out, in_37, in_45);
  and and_28 (and_28_out, in_37, in_45);
  and and_29 (and_29_out, or_11_out, xor_26_out);
  and and_30 (and_30_out, or_12_out, xor_28_out);
  xor xor_27 (xor_27_out, in_21, in_29);
  and and_31 (and_31_out, in_21, in_29);
  xor xor_28 (xor_28_out, in_53, in_61);
  and and_32 (and_32_out, in_53, in_61);
  xor xor_29 (out_71, xor_25_out, or_9_out);
  or or_13 (or_13_out, and_25_out, and_26_out);
  or or_14 (or_14_out, and_31_out, and_27_out);
  xor xor_30 (out_87, xor_26_out, or_11_out);
  or or_15 (or_15_out, and_28_out, and_29_out);
  or or_16 (or_16_out, and_32_out, and_30_out);
  xor xor_31 (out_79, xor_27_out, or_10_out);
  xor xor_32 (out_95, xor_28_out, or_12_out);
  and and_33 (and_33_out, or_13_out, xor_33_out);
  and and_34 (and_34_out, or_15_out, xor_35_out);
  xor xor_33 (xor_33_out, in_4, in_12);
  and and_35 (and_35_out, in_4, in_12);
  xor xor_34 (xor_34_out, in_20, in_28);
  and and_36 (and_36_out, in_20, in_28);
  and and_37 (and_37_out, or_14_out, xor_34_out);
  xor xor_35 (xor_35_out, in_36, in_44);
  and and_38 (and_38_out, in_36, in_44);
  xor xor_36 (xor_36_out, in_52, in_60);
  and and_39 (and_39_out, in_52, in_60);
  and and_40 (and_40_out, or_16_out, xor_36_out);
  or or_17 (or_17_out, and_35_out, and_33_out);
  or or_18 (or_18_out, and_38_out, and_34_out);
  xor xor_37 (out_70, xor_33_out, or_13_out);
  xor xor_38 (out_78, xor_34_out, or_14_out);
  or or_19 (or_19_out, and_36_out, and_37_out);
  xor xor_39 (out_86, xor_35_out, or_15_out);
  xor xor_40 (out_94, xor_36_out, or_16_out);
  or or_20 (or_20_out, and_39_out, and_40_out);
  and and_41 (and_41_out, or_17_out, xor_41_out);
  and and_42 (and_42_out, or_18_out, xor_43_out);
  xor xor_41 (xor_41_out, in_2, in_9);
  and and_43 (and_43_out, in_2, in_9);
  xor xor_42 (xor_42_out, in_18, in_25);
  and and_44 (and_44_out, in_18, in_25);
  and and_45 (and_45_out, or_19_out, xor_42_out);
  xor xor_43 (xor_43_out, in_34, in_41);
  and and_46 (and_46_out, in_34, in_41);
  xor xor_44 (xor_44_out, in_50, in_57);
  and and_47 (and_47_out, in_50, in_57);
  and and_48 (and_48_out, or_20_out, xor_44_out);
  or or_21 (or_21_out, and_43_out, and_41_out);
  or or_22 (or_22_out, and_46_out, and_42_out);
  xor xor_45 (out_68, xor_41_out, or_17_out);
  xor xor_46 (out_76, xor_42_out, or_19_out);
  or or_23 (or_23_out, and_44_out, and_45_out);
  xor xor_47 (out_84, xor_43_out, or_18_out);
  xor xor_48 (out_92, xor_44_out, or_20_out);
  or or_24 (or_24_out, and_47_out, and_48_out);
  and and_49 (and_49_out, or_21_out, xor_49_out);
  and and_50 (and_50_out, or_23_out, xor_50_out);
  and and_51 (and_51_out, or_22_out, xor_51_out);
  and and_52 (and_52_out, or_24_out, xor_52_out);
  xor xor_49 (xor_49_out, in_3, in_10);
  and and_53 (and_53_out, in_3, in_10);
  xor xor_50 (xor_50_out, in_19, in_26);
  and and_54 (and_54_out, in_19, in_26);
  xor xor_51 (xor_51_out, in_35, in_42);
  and and_55 (and_55_out, in_35, in_42);
  xor xor_52 (xor_52_out, in_51, in_58);
  and and_56 (and_56_out, in_51, in_58);
  or or_25 (or_25_out, and_53_out, and_49_out);
  or or_26 (or_26_out, and_54_out, and_50_out);
  or or_27 (or_27_out, and_55_out, and_51_out);
  or or_28 (or_28_out, and_56_out, and_52_out);
  xor xor_53 (out_69, xor_49_out, or_21_out);
  xor xor_54 (out_77, xor_50_out, or_23_out);
  xor xor_55 (out_85, xor_51_out, or_22_out);
  xor xor_56 (out_93, xor_52_out, or_24_out);
  and and_57 (and_57_out, or_25_out, xor_57_out);
  and and_58 (and_58_out, or_26_out, xor_58_out);
  and and_59 (and_59_out, or_27_out, xor_59_out);
  and and_60 (and_60_out, or_28_out, xor_60_out);
  xor xor_57 (xor_57_out, in_1, in_6);
  and and_61 (and_61_out, in_1, in_6);
  xor xor_58 (xor_58_out, in_17, in_22);
  and and_62 (and_62_out, in_17, in_22);
  xor xor_59 (xor_59_out, in_33, in_38);
  and and_63 (and_63_out, in_33, in_38);
  xor xor_60 (xor_60_out, in_49, in_54);
  and and_64 (and_64_out, in_49, in_54);
  or or_29 (or_29_out, and_61_out, and_57_out);
  or or_30 (or_30_out, and_62_out, and_58_out);
  or or_31 (or_31_out, and_63_out, and_59_out);
  or or_32 (out_99, and_64_out, and_60_out);
  xor xor_61 (out_67, xor_57_out, or_25_out);
  xor xor_62 (out_75, xor_58_out, or_26_out);
  xor xor_63 (out_83, xor_59_out, or_27_out);
  xor xor_64 (out_91, xor_60_out, or_28_out);

  // Other names for the same wires on the sheet: A0 = DataA[0]; A1 = DataA[1]; A2 = DataA[2]; A3 = DataA[3];
  //   A4 = DataA[4]; A5 = DataA[5]; A6 = DataA[6]; A7 = DataA[7]; A8 = DataA[8]; A9 = DataA[9]; A10 = DataA[10];
  //   A11 = DataA[11]; A12 = DataA[12]; A13 = DataA[13]; A14 = DataA[14]; A15 = DataA[15]; A16 = DataA[16];
  //   A17 = DataA[17]; A18 = DataA[18]; A19 = DataA[19]; A20 = DataA[20]; A21 = DataA[21]; A22 = DataA[22];
  //   A23 = DataA[23]; A24 = DataA[24]; A25 = DataA[25]; A26 = DataA[26]; A27 = DataA[27]; A28 = DataA[28];
  //   A29 = DataA[29]; A30 = DataA[30]; A31 = DataA[31]; B0 = DataB[0]; B1 = DataB[1]; B2 = DataB[2]; B3 = DataB[3];
  //   B4 = DataB[4]; B5 = DataB[5]; B6 = DataB[6]; B7 = DataB[7]; B8 = DataB[8]; B9 = DataB[9]; B10 = DataB[10];
  //   B11 = DataB[11]; B12 = DataB[12]; B13 = DataB[13]; B14 = DataB[14]; B15 = DataB[15]; B16 = DataB[16];
  //   B17 = DataB[17]; B18 = DataB[18]; B19 = DataB[19]; B20 = DataB[20]; B21 = DataB[21]; B22 = DataB[22];
  //   B23 = DataB[23]; B24 = DataB[24]; B25 = DataB[25]; B26 = DataB[26]; B27 = DataB[27]; B28 = DataB[28];
  //   B29 = DataB[29]; B30 = DataB[30]; B31 = DataB[31]
endmodule

module Test (
  output beq
);

  wire i0T, i1T, i2T, i3T, i4T, i5T, i6T;

  and and_1 (beq, i6T, i5T, ~i4T, ~i3T, i2T, i1T, i0T);  // AND_Gate
endmodule

module ControlLogic (
  input  [31:0] Instruction,
  output [3:0] ALUselecting,
  output RegWen
);

  wire orT, subT;

  and and_1 (ALUselecting[3], ~Instruction[2], ~Instruction[3], Instruction[4], Instruction[5], ~Instruction[6], ~Instruction[12], ~Instruction[13], ~Instruction[14], ~Instruction[30]);  // AND_Gate
  and and_2 (subT, ~Instruction[2], ~Instruction[3], Instruction[4], Instruction[5], ~Instruction[6], Instruction[12], ~Instruction[13], ~Instruction[14], ~Instruction[30]);  // AND_Gate
  and and_3 (orT, ~Instruction[2], ~Instruction[3], Instruction[4], Instruction[5], ~Instruction[6], Instruction[12], ~Instruction[13], Instruction[14], ~Instruction[30]);  // AND_Gate
  and and_4 (ALUselecting[1], ~Instruction[2], ~Instruction[3], Instruction[4], Instruction[5], ~Instruction[6], ~Instruction[12], Instruction[13], Instruction[14], ~Instruction[30]);  // AND_Gate
  or or_1 (ALUselecting[0], subT, orT);
  or or_2 (ALUselecting[2], orT, ALUselecting[1]);
  or or_3 (RegWen, ALUselecting[3], subT, orT, ALUselecting[1]);

  // Other names for the same wires on the sheet: A0T = ALUselecting[0]; A1T = ALUselecting[1]; andT = ALUselecting[1];
  //   A2T = ALUselecting[2]; A3T = ALUselecting[3]; addT = ALUselecting[3]; i2T = Instruction[2];
  //   i3T = Instruction[3]; i4T = Instruction[4]; i5T = Instruction[5]; i6T = Instruction[6]; i12T = Instruction[12];
  //   i13T = Instruction[13]; i14T = Instruction[14]; i30T = Instruction[30]
endmodule

module DataPath (
  output [31:0] Outt
);

  wire clock_1_out, controllogic_1_regwen;
  wire [3:0] controllogic_1_aluselecting;
  wire [4:0] rsplitor_1_rd, rsplitor_1_rs1, rsplitor_1_rs2;
  wire [31:0] registerfile_1_rs1, registerfile_1_rs2;

  Clock clock_1 (.out(clock_1_out));
  Rsplitor rsplitor_1 (
    .Instruction({32{1'b1}}), .rd(rsplitor_1_rd), .rs1(rsplitor_1_rs1), .rs2(rsplitor_1_rs2));  // open: opcode, funct3, funct7
  RegisterFile registerfile_1 (
    .rsi1(rsplitor_1_rs1), .rsi2(rsplitor_1_rs2), .rdi(rsplitor_1_rd), .rd(Outt), .we(controllogic_1_regwen),
    .Clk(clock_1_out), .rs1(registerfile_1_rs1), .rs2(registerfile_1_rs2));
  ControlLogic controllogic_1 (
    .Instruction({32{1'b1}}), .ALUselecting(controllogic_1_aluselecting), .RegWen(controllogic_1_regwen));
  ALU alu_1 (
    .DataA(registerfile_1_rs1), .DataB(registerfile_1_rs2), .Selecting(controllogic_1_aluselecting),
    .DataD(Outt));
endmodule

module ControlLogicROM (
  input  [31:0] Instruction,
  output [3:0] ALUselecting,
  output RegWen,
  output wbselect,
  output Bselect,
  output [2:0] immSelect,
  output [2:0] lselect,
  output WEmem,
  output BEQ
);

  ROM #(.addrWidth(9), .dataWidth(13)) rom_1 (
    .addr({Instruction[30], Instruction[14:12], Instruction[6:2]}),
    .data({lselect, wbselect, ALUselecting, RegWen, immSelect, Bselect}));
  and and_1 (WEmem, ~Instruction[6], Instruction[5], Instruction[4], ~Instruction[3], ~Instruction[2], Instruction[1], Instruction[0]);  // AND_Gate
  and and_2 (BEQ, Instruction[6], Instruction[5], ~Instruction[4], ~Instruction[3], ~Instruction[2], Instruction[1], Instruction[0]);  // AND_Gate

  // Other names for the same wires on the sheet: i2T = Instruction[2]; i3T = Instruction[3]; i4T = Instruction[4];
  //   i5T = Instruction[5]; i6T = Instruction[6]; i12T = Instruction[12]; i13T = Instruction[13];
  //   i14T = Instruction[14]; i30T = Instruction[30]; BselectT = Bselect; is0T = immSelect[0]; is1T = immSelect[1];
  //   is2T = immSelect[2]; A0T = ALUselecting[0]; A1T = ALUselecting[1]; A2T = ALUselecting[2]; A3T = ALUselecting[3];
  //   lselect0T = lselect[0]; lselect1T = lselect[1]; lselect2T = lselect[2]; i0T = Instruction[0];
  //   i1T = Instruction[1]

  // Notes on the sheet:
  //   contents of rom_1 (hex, n*v repeats v):
  //   11 0 0 0 211 7*0 210 19*0 411 0 0 0 231 7*0 230 19*0 811 0 0 0 251 7*0 250 23*0 271 7*0 270 19*0
  //   1011 0 0 0 291 7*0 290 19*0 1411 0 0 0 2b1 7*0 2b0 23*0 2d1 7*0 2d0 23*0 2f1 7*0 2f0 31*0 310 151*0
  //   3b1 7*0 3b0
endmodule

module ALUCtl (
  input  [31:0] rs2,
  input  [31:0] imm31_0,
  input  Bselect,
  output [31:0] DataB
);

  Multiplexer #(.width(32)) multiplexer_1 (.in0(rs2), .in1(imm31_0), .out(DataB), .sel(Bselect));
endmodule

module LoadByte (
  input  [31:0] A,
  input  [31:0] lw,
  output [31:0] LoadB,
  output [31:0] LoadBU
);

  wire [4:0] bitselector_1_out;
  wire [7:0] bitselector_2_out;
  wire [31:0] and_1_out, shifter_1_out, shifter_2_out, subtractor_1_out;

  assign and_1_out = A & 32'h3;  // AND_Gate and_1, 32 bits wide
  Subtractor #(.width(32)) subtractor_1 (.a(32'h3), .b(and_1_out), .out(subtractor_1_out));  // open: bin, bout
  BitSelector #(.group(5), .width(32)) bitselector_1 (.in(shifter_1_out), .out(bitselector_1_out), .sel(3'b000));
  Shifter #(.width(32)) shifter_1 (.in(subtractor_1_out), .\dist (5'b00011), .out(shifter_1_out));
  Shifter #(.shift("lr"), .width(32)) shifter_2 (.in(lw), .\dist (bitselector_1_out), .out(shifter_2_out));
  assign LoadBU = 32'hff & shifter_2_out;  // AND_Gate and_2, 32 bits wide
  BitSelector #(.group(8), .width(32)) bitselector_2 (.in(shifter_2_out), .out(bitselector_2_out), .sel(2'b00));
  assign LoadB = {{24{bitselector_2_out[7]}}, bitselector_2_out};  // Bit_Extender bit_extender_1

  // Other names for the same wires on the sheet: AT[31:0] = A; LoadByte[31:0] = LoadB; LoadbyteUnsignT[31:0] = LoadBU;
  //   lwT[31:0] = lw
endmodule

module Loadhalf (
  input  [31:0] A,
  input  [31:0] lw,
  output [31:0] LoadH,
  output [31:0] LoadHU
);

  wire bitselector_2_out;
  wire [15:0] bitselector_1_out;

  BitSelector #(.group(16), .width(32)) bitselector_1 (.in(lw), .out(bitselector_1_out), .sel(bitselector_2_out));
  BitSelector #(.width(32)) bitselector_2 (.in(A), .out(bitselector_2_out), .sel(5'b00001));
  assign LoadH = {{16{bitselector_1_out[15]}}, bitselector_1_out};  // Bit_Extender bit_extender_1
  assign LoadHU = {{16{1'b0}}, bitselector_1_out};  // Bit_Extender bit_extender_2

  // Other names for the same wires on the sheet: AT[31:0] = A; LoadhalfT[31:0] = LoadH;
  //   LoadhalfunsignT[31:0] = LoadHU; lwT[31:0] = lw
endmodule

module LoadCrtl (
  input  [31:0] A,
  input  [31:0] lw,
  input  [2:0] lSelect,
  input  wbselect,
  output [31:0] Data
);

  wire [31:0] Loadb, LoadbyteUnsignT, LoadhalfT, LoadhalfunsignT, multiplexer_1_out;

  Multiplexer #(.select(3), .width(32)) multiplexer_1 (
    .in0(Loadb), .in1(LoadhalfT), .in2(lw), .in4(LoadbyteUnsignT), .in5(LoadhalfunsignT),
    .out(multiplexer_1_out), .sel(lSelect));  // open: in3, in6, in7
  LoadByte loadbyte_1 (.A(A), .lw(lw), .LoadB(Loadb), .LoadBU(LoadbyteUnsignT));
  Loadhalf loadhalf_1 (.A(A), .lw(lw), .LoadH(LoadhalfT), .LoadHU(LoadhalfunsignT));
  Multiplexer #(.width(32)) multiplexer_2 (.in0(multiplexer_1_out), .in1(A), .out(Data), .sel(wbselect));

  // Other names for the same wires on the sheet: AT[31:0] = A; DT[31:0] = Data; lSelectT[2:0] = lSelect;
  //   lwT[31:0] = lw; wbSelectT = wbselect
endmodule

module IM (
  input  [31:0] ADDR,
  output [31:0] out_2
);

  ROM #(.addrWidth(16), .dataWidth(32)) rom_1 (.addr(ADDR[15:0]), .data(out_2));
endmodule

module Zeroflag (
  input  [31:0] inputZero,
  output zero_Flag
);

  nor nor_1 (zero_Flag, inputZero[0], inputZero[1], inputZero[2], inputZero[3], inputZero[4], inputZero[5], inputZero[6], inputZero[7], inputZero[8], inputZero[9], inputZero[10], inputZero[11], inputZero[12], inputZero[13], inputZero[14], inputZero[15], inputZero[16], inputZero[17], inputZero[18], inputZero[19], inputZero[20], inputZero[21], inputZero[22], inputZero[23], inputZero[24], inputZero[25], inputZero[26], inputZero[27], inputZero[28], inputZero[29], inputZero[30], inputZero[31]);
endmodule
